// Logisim project bitwright.circ as structural Verilog: 1 circuit, main circuit M0Workbench
module M0Workbench (
  input  Reset,
  input  Clear,
  input  Ack,
  input  OverflowClear,
  input  [6:0] X,
  input  [6:0] Y,
  input  [2:0] Color,
  input  Plot,
  output MouseValid,
  output [6:0] MouseX,
  output [6:0] MouseY,
  output [2:0] MouseButtons,
  output MouseOverflow
);

  wire Available, CanvasPlot, Clock, MouseDrawing, PixelClock, VideoReset;
  wire [6:0] ASCII;

  Clock #(.highDuration(1), .lowDuration(1)) HostClock (.out(Clock));
  not not_1 (PixelClock, Clock);
  Keyboard #(.buflen(32), .trigger("rising")) keyboard_1 (
    .clk(Clock), .re(Available), .clr(Reset), .avail(Available), .data(ASCII));
  // RGB_Video #(.width(128), .height(128), .scale(1), .cursor("No Cursor"), .reset("Asynchronous")) rgb_video_1: pin names not known; wires that end beside it: VideoReset, PixelClock, Plot, X, Y, Color
  or or_1 (VideoReset, Reset, Clear);
  and and_1 (MouseDrawing, MouseValid, MouseButtons[0]);
  TTY #(.rows(6), .cols(28), .trigger("rising")) tty_1 (.data(ASCII), .clk(Clock), .we(Available), .clr(Reset));
  and and_2 (CanvasPlot, MouseDrawing, Plot);
  // BitwrightCanvas bitwrightcanvas_1: pin names not known; wires that end beside it: Clock, Reset, CanvasPlot, Clear, MouseX, MouseY, Color, Ack, OverflowClear, MouseValid, MouseX, MouseY, MouseButtons, MouseOverflow

  // Other names for the same wires on the sheet: PrimaryDown = MouseButtons[0]

  // Notes on the sheet:
  //   BITWRIGHT M0 / host I/O feasibility workbench
  //   No CPU or circuit FIFO yet. Host adapters are visibly separate. Use the Poke tool; enable ticks for live echo / mouse.
  //   Reset clears host state. Ack held high drains mouse packets one per falling edge.
  //   Ack low preserves the front packet while mouse events queue; outputs on the right show it.
  //   Manual pixel inputs for the stock display
  //   ASCII Keyboard -> TTY / both sample on rising edges
  //   Stock RGB Video
  //   Host bridge: retained pixels + press / drag / release
  //   Mouse events only: this is the host queue, not the future machine's 16-event FIFO.
  //   To paint: set Color, Plot=1, Ack=1; enable ticks and press / drag on the canvas.
  //   Gates echo coordinates to the pixel bus; the bridge only obeys bus commands.
endmodule
